// Logisim project fizz.circ as structural Verilog: 3 circuits, main circuit main
module main (
);

  wire and_1_out, mips_alu_4_bit_1_p5, registers_1_p2, registers_1_p5, undriven_3, undriven_4, undriven_5,
       undriven_6, undriven_7, undriven_9, xor_1_out;
  wire [1:0] undriven;
  wire [3:0] demultiplexer_1_out1, multiplexer_1_out, registers_1_p4, rom_3_data;
  wire [7:0] adder_1_out, adder_2_out, mips_alu_4_bit_1_p6, multiplexer_2_out, multiplexer_4_out, ram_1_data,
       register_1_q, registers_1_p1, registers_1_p6, undriven_2, undriven_8;
  wire [11:4] demultiplexer_1_out1_2;
  wire [15:0] demultiplexer_1_out2, mips_alu_4_bit_1_p7;
  wire [19:0] rom_1_data;

  Register register_1 (.D(multiplexer_4_out), .Q(register_1_q));  // open: en, clk, clr
  Adder adder_1 (.a(8'h1), .b(register_1_q), .out(adder_1_out));  // open: cin, cout
  ROM #(.dataWidth(20)) rom_1 (.addr(register_1_q), .data(rom_1_data));  // open: sel
  ROM #(.addrWidth(4), .dataWidth(4)) rom_2 ();  // open: addr, data, sel
  // Registers registers_1: pin names not known; wires that end beside it: registers_1_p1, registers_1_p2, demultiplexer_1_out1_2[11:8], registers_1_p4, registers_1_p5, registers_1_p6
  Multiplexer #(.width(4)) multiplexer_1 (
    .in1(demultiplexer_1_out1), .out(multiplexer_1_out), .sel(undriven[0]));  // open: in0, en
  ROM #(.addrWidth(4), .dataWidth(4)) rom_3 (.addr(rom_1_data[3:0]), .data(rom_3_data));  // open: sel
  // MIPS_ALU_4_bit mips_alu_4_bit_1: pin names not known; wires that end beside it: registers_1_p5, registers_1_p6, multiplexer_1_out, rom_3_data, mips_alu_4_bit_1_p5, mips_alu_4_bit_1_p6, mips_alu_4_bit_1_p7
  Demultiplexer #(.select(2), .width(16)) demultiplexer_1 (
    .out0(mips_alu_4_bit_1_p7), .out1({registers_1_p4, demultiplexer_1_out1_2, demultiplexer_1_out1}),
    .out2(demultiplexer_1_out2), .in(rom_1_data[19:4]), .sel(undriven));  // open: out3, en
  Adder adder_2 (.a(adder_1_out), .b(undriven_2), .out(adder_2_out));  // open: cin, cout
  xor xor_1 (xor_1_out, mips_alu_4_bit_1_p5, undriven_3);
  RAM #(.bus("separate")) ram_1 (
    .addr(mips_alu_4_bit_1_p6), .din(registers_1_p6), .data(ram_1_data), .str(undriven_4), .ld(undriven_5));  // open: sel, clk, clr
  Multiplexer #(.width(8)) multiplexer_2 (
    .in0(adder_1_out), .in1(adder_2_out), .out(multiplexer_2_out), .sel(and_1_out));  // open: en
  and and_1 (and_1_out, xor_1_out, undriven_6);
  Multiplexer #(.width(8)) multiplexer_3 (
    .in0(mips_alu_4_bit_1_p6), .in1(ram_1_data), .out(registers_1_p1), .sel(undriven_7));  // open: en
  Multiplexer #(.width(8)) multiplexer_4 (
    .in0(multiplexer_2_out), .in1(undriven_8), .out(multiplexer_4_out), .sel(undriven_9));  // open: en

  // Notes on the sheet:
  //   PC
  //   opcode
  //   contents of rom_2 (hex, n*v repeats v):
  //   f 6 6 2 6 2 2 2 1 8 9 6 c 0 1
  //   MAKE ALU 8 BIT AGAIN
  //   contents of rom_3 (hex, n*v repeats v):
  //   f 6 6 2 6 2 2 2 1 8 9 6 c 0 1
  //   branching
  //   i type
  //   j type
  //   jump
  //   src 2
  //   src 1
  //   branch address
  //   MEM WRITE
  //   bneq
  //   MEM READ
  //   bneq OR beq
  //   JUMP ADDRESS
  //   MEM TO REG
  //   JUMP
endmodule

module ALU (
  input  [7:0] in_1,
  input  [7:0] in_2,
  input  [2:0] in_3,
  output [7:0] out_4
);

  wire [7:0] adder_1_out, and_1_out, nor_1_out, or_1_out, subtractor_1_out;

  Adder adder_1 (.a(in_1), .b(in_2), .out(adder_1_out));  // open: cin, cout
  Subtractor subtractor_1 (.a(in_1), .b(in_2), .out(subtractor_1_out));  // open: bin, bout
  assign and_1_out = in_1 & in_2;  // AND_Gate and_1, 8 bits wide
  assign or_1_out = in_1 | in_2;  // OR_Gate or_1, 8 bits wide
  assign nor_1_out = ~(in_1 | in_2);  // NOR_Gate nor_1, 8 bits wide
  Multiplexer #(.select(3), .width(8)) multiplexer_1 (
    .in0(adder_1_out), .in1(subtractor_1_out), .in2(and_1_out), .in3(or_1_out), .in4(nor_1_out), .out(out_4),
    .sel(in_3));  // open: in5, in6, in7, en
endmodule

module Registers (
  input  clock,
  input  [7:0] data_in,
  input  regWrite,
  input  [3:0] addressA___R_W,
  input  [3:0] addressB__ReadOnly,
  output [7:0] data_out_A,
  output [7:0] data_out_B
);

  wire demultiplexer_1_out0, demultiplexer_1_out1, demultiplexer_1_out2, demultiplexer_1_out3,
       demultiplexer_1_out4, demultiplexer_1_out14;
  wire [7:0] t0_q, t1_q, t2_q, t3_q, t4_q, ZERO_q;

  Demultiplexer #(.select(4)) demultiplexer_1 (
    .out0(demultiplexer_1_out0), .out1(demultiplexer_1_out1), .out2(demultiplexer_1_out2),
    .out3(demultiplexer_1_out3), .out4(demultiplexer_1_out4), .out14(demultiplexer_1_out14),
    .out15(demultiplexer_1_out14), .in(regWrite), .sel(addressA___R_W));  // open: out5, out6, out7, out8, out9, out10, out11, out12, out13, en
  Register t0 (.D(data_in), .en(demultiplexer_1_out0), .Q(t0_q), .clk(clock));  // open: clr
  Register t1 (.D(data_in), .en(demultiplexer_1_out1), .Q(t1_q), .clk(clock));  // open: clr
  Register t2 (.D(data_in), .en(demultiplexer_1_out3), .Q(t2_q), .clk(clock));  // open: clr
  Register t3 (.D(data_in), .en(demultiplexer_1_out2), .Q(t3_q), .clk(clock));  // open: clr
  Register t4 (.D(data_in), .en(demultiplexer_1_out4), .Q(t4_q), .clk(clock));  // open: clr
  Register ZERO (.D({8{1'b0}}), .en(demultiplexer_1_out14), .Q(ZERO_q), .clk(clock));  // open: clr
  Multiplexer #(.select(4), .width(8), .enable("false")) multiplexer_1 (
    .in0(t0_q), .in1(t1_q), .in2(t2_q), .in3(t3_q), .in4(t4_q), .in15(ZERO_q), .out(data_out_A),
    .sel(addressA___R_W));  // open: in5, in6, in7, in8, in9, in10, in11, in12, in13, in14
  Multiplexer #(.select(4), .width(8)) multiplexer_2 (
    .in0(t0_q), .in1(t1_q), .in2(t2_q), .in3(t3_q), .in4(t4_q), .in15(ZERO_q), .out(data_out_B),
    .sel(addressB__ReadOnly));  // open: in5, in6, in7, in8, in9, in10, in11, in12, in13, in14, en
endmodule
